// Logisim project Basic Logic Devices.circ as structural Verilog: 1 circuit, main circuit main
module main (
  input  I0,
  input  in_2,
  input  I1,
  input  in_4,
  input  I2,
  input  I0_2,
  input  in_7,
  input  I1_2,
  input  I3,
  input  in_10,
  input  in_11,
  input  [1:0] in_12,
  input  in_13,
  input  in_14,
  input  in_15,
  input  in_16,
  input  [2:0] in_17,
  input  in_18,
  input  in_19,
  input  in_20,
  output F,
  output F_2,
  output out_23
);

  Multiplexer multiplexer_1 (.in0(I0_2), .in1(I1_2), .out(out_23), .sel(in_16), .en(in_13));
  Multiplexer #(.select(2)) multiplexer_2 (.in0(I0), .in1(I1), .in2(I2), .in3(I3), .out(F), .sel(in_12), .en(in_10));
  Multiplexer #(.select(3)) multiplexer_3 (
    .in0(in_2), .in1(in_4), .in2(in_7), .in3(in_11), .in4(in_14), .in5(in_18), .in6(in_19), .in7(in_20),
    .out(F_2), .sel(in_17), .en(in_15));

  // Notes on the sheet:
  //   2: 1 MUX
  //   A
  //   F
  //   A B
  //   4:1 MUX
  //   (3 variable logic expression)
  //   8:1 MUX
  //   (4 variable logic expression)
endmodule
