// Logisim project FF.circ as structural Verilog: 1 circuit, main circuit main
module main (
  input  in_1,
  input  in_2,
  input  in_3,
  input  in_4,
  input  in_5,
  input  in_6,
  input  in_7,
  input  in_8,
  output out_9,
  output out_10,
  output out_11,
  output out_12,
  output out_13,
  output out_14
);

  wire clock_1_out, clock_2_out, clock_3_out, clock_4_out, clock_5_out, clock_6_out, not_1_out, not_2_out,
       not_3_out;

  Clock clock_1 (.out(clock_1_out));
  Clock clock_2 (.out(clock_2_out));
  Clock clock_3 (.out(clock_3_out));
  J_K_Flip_Flop j_k_ff_1 (.J(in_1), .clk(clock_1_out), .K(in_3), .Q(out_9));  // open: Qn, preset, en, reset
  T_Flip_Flop t_ff_1 (.clk(clock_2_out), .T(in_5), .Q(out_11));  // open: Qn, preset, reset, en
  D_Flip_Flop d_ff_1 (.clk(clock_3_out), .D(in_7), .Q(out_13));  // open: Qn, preset, en, reset
  Clock clock_4 (.out(clock_4_out));
  Clock clock_5 (.out(clock_5_out));
  not not_1 (not_1_out, clock_4_out);
  Clock clock_6 (.out(clock_6_out));
  J_K_Flip_Flop j_k_ff_2 (.J(in_2), .clk(not_2_out), .K(in_4), .Q(out_10));  // open: Qn, preset, en, reset
  not not_2 (not_2_out, clock_5_out);
  T_Flip_Flop t_ff_2 (.clk(not_1_out), .T(in_6), .Q(out_12));  // open: Qn, preset, reset, en
  D_Flip_Flop d_ff_2 (.clk(not_3_out), .D(in_8), .Q(out_14));  // open: Qn, preset, en, reset
  not not_3 (not_3_out, clock_6_out);

  // Notes on the sheet:
  //   Rising
  //   J-K FF
  //   Rising T FF
  //   Rising D FF
  //   Falling
  //   Falling D FF
  //   J-K FF
  //   Falling T FF
endmodule
