// Logisim project LDDraft2.0.circ as structural Verilog: 1 circuit, main circuit main
module main (
  input  A,
  input  B,
  input  C
);

  wire nor_1_out, nor_2_out, nor_3_out, nor_4_out, nor_5_out, nor_6_out, nor_7_out, nor_8_out, nor_9_out,
       nor_10_out, nor_11_out, nor_12_out, nor_13_out, nor_14_out, nor_15_out, nor_16_out, nor_17_out,
       nor_18_out, nor_19_out, nor_20_out, not_1_out, not_2_out, not_3_out;

  not not_1 (not_1_out, A);
  not not_2 (not_2_out, B);
  not not_3 (not_3_out, C);
  nor nor_1 (nor_1_out, A, B);
  nor nor_2 (nor_2_out, not_2_out, not_3_out);
  nor nor_3 (nor_3_out, A, B);
  nor nor_4 (nor_4_out, not_3_out, not_3_out);
  nor nor_5 (nor_5_out, B, B);
  nor nor_6 (nor_6_out, C, C);
  nor nor_7 (nor_7_out, not_3_out, not_3_out);
  nor nor_8 (nor_8_out, not_2_out, not_2_out);
  nor nor_9 (nor_9_out, not_1_out, not_1_out);
  nor nor_10 (nor_10_out, not_2_out, not_2_out);
  nor nor_11 (nor_11_out, not_1_out, not_1_out);
  nor nor_12 (nor_12_out, not_2_out, not_2_out);
  nor nor_13 (nor_13_out, A, C);
  nor nor_14 (nor_14_out, nor_1_out, nor_1_out);
  nor nor_15 (nor_15_out, nor_2_out, nor_2_out);
  nor nor_16 (nor_16_out, nor_3_out, nor_4_out);
  nor nor_17 (nor_17_out, nor_5_out, nor_6_out);
  nor nor_18 (nor_18_out, nor_7_out, nor_8_out, nor_9_out);
  nor nor_19 (nor_19_out, nor_10_out, nor_11_out);
  nor nor_20 (nor_20_out, nor_12_out, nor_13_out);
  LED led_1 (.in(nor_14_out));
  LED led_2 (.in(nor_15_out));
  LED led_3 (.in(nor_16_out));
  LED led_4 (.in(nor_17_out));
  LED led_5 (.in(nor_18_out));
  LED led_6 (.in(nor_19_out));
  LED led_7 (.in(nor_20_out));
  LED led_8 (.in(nor_14_out));
  LED led_9 (.in(nor_19_out));
  LED led_10 (.in(1'b1));
  LED led_11 (.in(1'b1));
  LED led_12 (.in(1'b1));
  LED led_13 (.in(1'b1));
  LED led_14 (.in(1'b1));
  LED led_15 (.in(nor_17_out));
  LED led_16 (.in(nor_17_out));
  LED led_17 (.in(1'b1));
  LED led_18 (.in(1'b1));
  LED led_19 (.in(1'b1));
  LED led_20 (.in(1'b1));
  LED led_21 (.in(1'b0));
  LED led_22 (.in(1'b1));
  LED led_23 (.in(nor_16_out));
  LED led_24 (.in(nor_16_out));
  LED led_25 (.in(nor_14_out));
  LED led_26 (.in(nor_14_out));
  LED led_27 (.in(nor_14_out));
  LED led_28 (.in(1'b0));
  LED led_29 (.in(1'b0));
  LED led_30 (.in(nor_19_out));
  LED led_31 (.in(1'b0));
  LED led_32 (.in(nor_19_out));
  LED led_33 (.in(1'b0));
  LED led_34 (.in(nor_19_out));
  LED led_35 (.in(nor_18_out));
  LED led_36 (.in(1'b0));
  LED led_37 (.in(nor_19_out));
  LED led_38 (.in(nor_17_out));
  LED led_39 (.in(nor_17_out));
  LED led_40 (.in(1'b0));
  LED led_41 (.in(1'b0));
  LED led_42 (.in(nor_20_out));
  LED led_43 (.in(1'b0));
  LED led_44 (.in(nor_20_out));
  LED led_45 (.in(1'b0));
  LED led_46 (.in(nor_20_out));
  LED led_47 (.in(1'b0));
  LED led_48 (.in(1'b0));
  LED led_49 (.in(1'b0));
  LED led_50 (.in(1'b0));
  LED led_51 (.in(1'b0));
  LED led_52 (.in(nor_16_out));
  LED led_53 (.in(nor_16_out));
  LED led_54 (.in(nor_14_out));
  LED led_55 (.in(nor_14_out));
  LED led_56 (.in(1'b1));
  LED led_57 (.in(nor_18_out));
  LED led_58 (.in(1'b1));
  LED led_59 (.in(nor_18_out));
  LED led_60 (.in(1'b1));
  LED led_61 (.in(nor_18_out));
  LED led_62 (.in(1'b1));
  LED led_63 (.in(nor_18_out));
  LED led_64 (.in(1'b1));
  LED led_65 (.in(nor_17_out));
  LED led_66 (.in(nor_17_out));
  LED led_67 (.in(nor_15_out));
  LED led_68 (.in(nor_15_out));
  LED led_69 (.in(nor_15_out));
  LED led_70 (.in(nor_20_out));
  LED led_71 (.in(nor_15_out));
  LED led_72 (.in(nor_20_out));
  LED led_73 (.in(nor_15_out));
  LED led_74 (.in(nor_16_out));
  LED led_75 (.in(nor_16_out));

  // Notes on the sheet:
  //   Power
  //   Ground
  //   A'
  //   B'
  //   C'
  //   F1 + F2
  //   F4
  //   F5 + F6
  //   F9 + F10
  //   F13
  //   F14
  //   F15
  //   Power
  //   Ground
endmodule
