// Logisim project Logisim HEX Disp (1).circ as structural Verilog: 1 circuit, main circuit main
module main (
);

  wire undriven, undriven_2, undriven_3, undriven_4, undriven_5, undriven_6, undriven_7, undriven_8,
       undriven_9, undriven_10, undriven_11, undriven_12, undriven_13, undriven_14, undriven_15, undriven_16;

  LED led_1 (.in(undriven_5));
  LED led_2 (.in(undriven_5));
  LED led_3 (.in(undriven_5));
  LED led_4 (.in(undriven_5));
  LED led_5 (.in(undriven_5));
  LED led_6 (.in(undriven));
  LED led_7 (.in(undriven_6));
  LED led_8 (.in(undriven_6));
  LED led_9 (.in(undriven_6));
  LED led_10 (.in(undriven_6));
  LED led_11 (.in(undriven_6));
  LED led_12 (.in(undriven_2));
  LED led_13 (.in(undriven_3));
  LED led_14 (.in(undriven_3));
  LED led_15 (.in(undriven_3));
  LED led_16 (.in(undriven_8));
  LED led_17 (.in(undriven_4));
  LED led_18 (.in(undriven_8));
  LED led_19 (.in(undriven_4));
  LED led_20 (.in(undriven_8));
  LED led_21 (.in(undriven_4));
  LED led_22 (.in(undriven_8));
  LED led_23 (.in(undriven_4));
  LED led_24 (.in(undriven_8));
  LED led_25 (.in(undriven_4));
  LED led_26 (.in(undriven));
  LED led_27 (.in(undriven));
  LED led_28 (.in(undriven_7));
  LED led_29 (.in(undriven_9));
  LED led_30 (.in(undriven_7));
  LED led_31 (.in(undriven_9));
  LED led_32 (.in(undriven_7));
  LED led_33 (.in(undriven_9));
  LED led_34 (.in(undriven_7));
  LED led_35 (.in(undriven_9));
  LED led_36 (.in(undriven_7));
  LED led_37 (.in(undriven_9));
  LED led_38 (.in(undriven_2));
  LED led_39 (.in(undriven_2));
  LED led_40 (.in(undriven_12));
  LED led_41 (.in(undriven_12));
  LED led_42 (.in(undriven_12));
  LED led_43 (.in(undriven_14));
  LED led_44 (.in(undriven_14));
  LED led_45 (.in(undriven_14));
  LED led_46 (.in(undriven_14));
  LED led_47 (.in(undriven_14));
  LED led_48 (.in(undriven_13));
  LED led_49 (.in(undriven_13));
  LED led_50 (.in(undriven_13));
  LED led_51 (.in(undriven_10));
  LED led_52 (.in(undriven_15));
  LED led_53 (.in(undriven_10));
  LED led_54 (.in(undriven_15));
  LED led_55 (.in(undriven_10));
  LED led_56 (.in(undriven_15));
  LED led_57 (.in(undriven_10));
  LED led_58 (.in(undriven_15));
  LED led_59 (.in(undriven_10));
  LED led_60 (.in(undriven_15));
  LED led_61 (.in(undriven_11));
  LED led_62 (.in(undriven_11));
  LED led_63 (.in(undriven_11));
  LED led_64 (.in(undriven_16));
  LED led_65 (.in(undriven_16));
  LED led_66 (.in(undriven_16));
  LED led_67 (.in(undriven_16));
  LED led_68 (.in(undriven_16));
endmodule
