// Logisim project SR Latches.circ as structural Verilog: 1 circuit, main circuit main
module main (
  input  R,
  input  S,
  input  R_2,
  input  G,
  input  in_5,
  input  G_2,
  input  D,
  output Q,
  output Q_prime,
  output Q_2,
  output Q_prime_2,
  output Q_3,
  output Q_prime_3
);

  wire and_1_out, and_2_out, and_3_out, and_4_out, not_1_out;

  and and_1 (and_1_out, R_2, G);
  and and_2 (and_2_out, G, in_5);
  not not_1 (not_1_out, D);
  and and_3 (and_3_out, not_1_out, G_2);
  and and_4 (and_4_out, G_2, D);
  nor nor_1 (Q, R, Q_prime);
  nor nor_2 (Q_prime, Q, S);
  nor nor_3 (Q_2, and_1_out, Q_prime_2);
  nor nor_4 (Q_prime_2, Q_2, and_2_out);
  nor nor_5 (Q_3, and_3_out, Q_prime_3);
  nor nor_6 (Q_prime_3, Q_3, and_4_out);

  // Notes on the sheet:
  //   S
  //   Gated SR Latch
  //   Gated D Latch
  //   SR Latch
endmodule
